# Fritzing sketch toddleplayer (saved by Fritzing 0.9.3b)
stripboards: 2
perfboards: 3

parts:
  S5 = Toggle Switch [package=THT]  # not connected
  TRRS1 = Audio Jack (TRRS) 3.5mm [part_number="LUMBERG JEITA RC-5325A" package="RC-5325A [SMD]"]  # not connected
  SP1 = SPEAKER [package=pcb_mount_speaker]  # not connected
  SP2 = SPEAKER [package=pcb_mount_speaker]  # not connected
  S6 = Round Pushbutton
  Raspberry_Pi_Zero1 = Raspberry Pi Zero

nets:
  N1: S6.leg0, Raspberry_Pi_Zero1.GPIO16
  N2: S6.leg1, Raspberry_Pi_Zero1.GND

notes:
  PAM8403 3W Amplifier
  INR
  GND
  VCC
  INL
  5V Batterypack
  PHAT DAC
